# Fritzing sketch prototype_wiring (saved by Fritzing 1.0.7)

parts:
  A1 = XIAO NRF52840 sense tht
  Part1 = Adafruit NAU7802
  J2 = Camdenboss CTB0158-3 [part_number=CTB0158-3 package=THT]
  R1 = Resistor [tolerance=±5% power=0.25W resistance=4.7k package=THT]
  S1 = SPST Switch [package=switche-dpdt]

nets:
  N1: A1.Pin_5, J2.pin2, R1.Pin_0
  N2: A1.Pin_11, Part1.SCL
  N3: A1.Pin_12, S1.O
  N4: A1.Pin_13, A1.Pin_21, Part1.GND, J2.pin1
  N5: A1.Pin_16, Part1.SDA
  N6: A1.Pin_20, Part1.VCC, J2.pin3, R1.Pin_1

notes:
  D7
  D6
  D0
  https://de.aliexpress.com/item/1005008946041200.html?spm=a2g0o.productlist.main.5.6098Xvd9Xvd9R7&algo_pvid=b970cc30-7441-4f0d-a253-4636fe3d6967&algo_exp_id=b970cc30-7441-4f0d-a253-4636fe3d6967-4&pdp_ext_f=%7B%22order%22%3A%22-1%22%2C%22eval%22%3A%221%22%2C%22fromPage%22%3A%22search%22%7D&pdp_npi=6%40dis%21EUR%213.28%212.79%21%21%213.64%213.10%21%402103890917822896360728642ed9c5%2112000047308995871%21sea%21DE%21834912736%21X%211%210%21n_tag%3A-29919%3Bd%3Ab714ae0e%3Bm03_new_user%3A-29895&curPageLogUid=ZhT9T9jkvbcK&utparam-url=scene%3Asearch%7Cquery_from%3A%7Cx_object_id%3A1005008946041200%7C_p_origin_prod%3A

custom parts:
  XIAO NRF52840 sense tht: The Seeed Studio XIAO family, Seeed Studio XIAO nRF52840 is equipped with a powerful Nordic nRF52840 MCU which integrates Bluetooth 5.0 connectivity. This is the THT version there is also a SMD version of the part.
